# Fritzing sketch ArduinoWith2LightSensor (saved by Fritzing 0.9.1b)
circuit board: 8.46667cm x 5.64444cm
breadboards: 1

parts:
  Part1 = Arduino Uno (Rev3)
  R1 = Photocell (LDR) [package=THT]
  R2 = Photocell (LDR) [package=THT]
  R3 = Resistor [tolerance=±5% resistance=1k package=THT]
  R4 = Resistor [tolerance=±5% resistance=1k package=THT]
  LED1 = LED - 5mm [color="Red (633nm)" package="5 mm [THT]"]
  R5 = Resistor [tolerance=±5% resistance=560 package=THT]

nets (from the breadboard view):
  N1: Part1.A0, R2.pin_0, R4.Pin_1
  N2: Part1.A1, R1.pin_0, R3.Pin_1
  N3: Part1.D11_PWM/MOSI, LED1.anode
  N4: Part1.5V, R1.pin_1, R2.pin_1
  N5: Part1.GND, R3.Pin_0, R4.Pin_0, R5.Pin_0
  N6: LED1.cathode, R5.Pin_1
