# Fritzing sketch FingerDrumer (saved by Fritzing 0.9.1b)
breadboards: 1

parts:
  Part1 = Arduino Uno (Rev3) - ICSP
  U1 = MIDI_CONN_FEMALE_SUPPORT [package=din_5_female_support]
  R1 = Resistor [tolerance=±5% resistance=220 package="1206 [SMD]"]
  R4 = Resistor [tolerance=±5% resistance=1M package="1206 [SMD]"]
  J1 = Piezo Speaker

nets:
  N1: Part1.A0, R4.Pin_1, J1.pin2
  N2: Part1.5V, R1.Pin_1, R4.Pin_0, J1.pin1
  N3: Part1.D3_PWM, U1.MIDI_IN
  N4: Part1.GND, U1.NC1
  N5: U1.MIDI_OUT, R1.Pin_0
