# Fritzing sketch ArduinoAndDS18B20 (saved by Fritzing 0.9.1b)
breadboards: 1

parts:
  Part1 = Arduino Uno (Rev3)
  T1 = DS18B20 Temperature Sensor [package=Undefined]
  R1 = Resistor [tolerance=±5% resistance=10k package=THT]

nets:
  GND: Part1.GND, T1.GND
  N1: Part1.D3_PWM, T1.DQ, R1.Pin_1
  5V: Part1.5V, T1.Vdd, R1.Pin_0

custom parts:
  DS18B20 Temperature Sensor: The DS18B20 digital thermometer provides 9-bit to 12-bit Celsius temperature measurements and has an alarm function with nonvolatile userprogrammable upper and lower trigger points. The DS18B20 communicates over a 1-Wire bus that by definition requires only one data line (and ground) for communication with a central microprocessor. It has an operating temperature range of -55°C to +125°C and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
