# Fritzing sketch Timer 555 Project 1 (saved by Fritzing 0.9.1b)
breadboards: 1

parts:
  X1 = USB Connectors [package=usb-minib]
  U1 = 555 Timer [package="DIP8 [THT]"]  # not connected
  C1 = Electrolytic Capacitor [capacitance=470µF package="300 mil [THT, electrolytic]"]
  R1 = Resistor [tolerance=±5% resistance=47k package="0805 [SMD]"]
  S1 = Momentary Switch [package=ksa_sealed_tac_switch]
  R2 = Resistor [tolerance=±5% resistance=10k package="0805 [SMD]"]
  U2 = 555 Timer [package="DIP8 [THT]"]
  C2 = Electrolytic Capacitor [capacitance=47µF package="300 mil [THT, electrolytic]"]
  LED1 = LED - 5mm [color="Red (633nm)" package="5 mm [THT]"]
  J1 = Piezo Speaker
  R3 = Resistor [tolerance=±5% resistance=4.7k package="0805 [SMD]"]
  R4 = Resistor [tolerance=±5% resistance=4.7k package="0805 [SMD]"]
  R5 = PHOTOCELL [package=photocell-kit]

nets:
  N1: X1.D-, R1.Pin_1, R2.Pin_0, U2.Reset, J1.pin2
  N2: X1.VBUS, C1.-, S1.2, U2.Ground, C2.-, LED1.cathode
  N3: C1.+, R1.Pin_0
  N4: S1.3, R2.Pin_1
  N5: U2.Trigger, U2.Threshold, C2.+, R4.Pin_1
  N6: U2.Output, LED1.anode, J1.pin1
  N7: U2.Discharge, R3.Pin_0, R5.P$1
  N8: U2.Vcc_Supply_Voltage, R3.Pin_1
