# Fritzing sketch Timer555_2_Blinking_LEDs.SmoothBlinkOfBlueLight - Copy (saved by Fritzing 0.9.1b)
breadboards: 1

parts:
  U1 = 555 Timer [package="SO8 [SMD]"]
  R1 = Resistor [tolerance=±5% resistance=220k package=THT]
  C1 = Electrolytic Capacitor [capacitance=47µF package="0605 [SMD, electrolytic]"]
  R2 = Resistor [tolerance=±5% resistance=10k package=THT]
  R3 = Resistor [tolerance=±5% resistance=220 package=THT]
  LED1 = smd LED [color="Red (633nm)" package="0805 [SMD]"]
  LED2 = smd LED [color="Blue (505nm)" package="0805 [SMD]"]
  R5 = Resistor [tolerance=±5% resistance=10k package=THT]
  C3 = Electrolytic Capacitor [capacitance=470µF voltage=10V package="300 mil [THT, electrolytic]"]

nets:
  N1: U1.Pin_1, C1.-, LED2.cathode, C3.-
  N2: U1.Pin_2, U1.Pin_6, C1.+, R2.Pin_1
  N3: U1.Pin_3, R3.Pin_1, R5.Pin_1
  N4: U1.Pin_4, U1.Pin_8, R1.Pin_1, LED1.anode
  N5: U1.Pin_7, R1.Pin_0, R2.Pin_0
  N6: R3.Pin_0, LED1.cathode
  N7: LED2.anode, R5.Pin_0, C3.+

// code stored in the sketch: Timer555_2_Blinking_LEDs.ino
/*
1. Pin1 to ground
2. Pin2(trigger) to pin6(Threshold)
3. Pin8(Vcc) to pin4(Reset)
4. Pin7(Discharge) to pin8(Vcc) using 22k Ohm resistor
5. Connect 47uF Capacitor negative pin to ground and positive pin to pin6 (threshold)
6. Connect 47uF Capacitor positive pin to pin6 (threshold)
7. Connect 47uF Capacitor positive pin to pin7(Discharge) using 10k Ohm resistor
8. Connectpin3(Output) to Empty Row
	8.1 Empty row -> 200Ohm Resistor -> -LED1 -> LED1+ -> Vcc
	8.1 Empty row -> 200Ohm Resistor -> +LED2 -> LED2-> Ground
9. Connect Pin8(Vcc) to Power
*/
